# Fritzing sketch serverraumüberwachung (saved by Fritzing 1.0.1rc)
breadboards: 1

parts:
  Part1 = Arduino Mega ADK (Rev3)
  HC-SR04_Sensor_1 = HC-SR04 Ultrasonic Distance Sensor
  F1 = Fan - Ventilador [package=THT]
  DHT11_1 = DHT11 module
  U1 = LCD-16X2 [package=lcd-16x2_noholes]
  LCM1602_IIC2 = LCM1602 IIC [part_number="LCM1602 IIC" chip_label="LCM1602 IIC" package="DIP (Dual Inline) [THT]"]

nets:
  N1: Part1.D21/SCL, LCM1602_IIC2.SCL
  N2: Part1.D20/SDA, LCM1602_IIC2.SDA
  GND: Part1.GND, HC-SR04_Sensor_1.GND, F1.GND, DHT11_1.GND, LCM1602_IIC2.GND
  N3: Part1.D9_PWM, F1.5V
  N4: Part1.D2_PWM, DHT11_1.DATA
  N5: Part1.D3_PWM, HC-SR04_Sensor_1.TRIG
  N6: Part1.D4_PWM, HC-SR04_Sensor_1.ECHO
  VCC: Part1.5V, HC-SR04_Sensor_1.VCC, DHT11_1.VCC, LCM1602_IIC2.VCC
  VSS: U1.VSS, LCM1602_IIC2.VSS
  VDD: U1.VDD, LCM1602_IIC2.VDD
  N7: U1.VO, LCM1602_IIC2.V0
  N8: U1.RS, LCM1602_IIC2.RS
  N9: U1.R_W, LCM1602_IIC2.RW
  N10: U1.E, LCM1602_IIC2.E
  N11: U1.DB0, LCM1602_IIC2.D0
  N12: U1.DB1, LCM1602_IIC2.D1
  N13: U1.DB2, LCM1602_IIC2.D2
  N14: U1.DB3, LCM1602_IIC2.D3
  N15: U1.DB4, LCM1602_IIC2.D4
  N16: U1.DB5, LCM1602_IIC2.D5
  N17: U1.DB6, LCM1602_IIC2.D6
  N18: U1.DB7, LCM1602_IIC2.D7
  N19: U1.A, LCM1602_IIC2.A
  N20: U1.K, LCM1602_IIC2.K
  N21: LCM1602_IIC2.LED_A, LCM1602_IIC2.LED_B

custom parts:
  Fan - Ventilador: Ventilador de 2 pines, se encuentra comunmente en computadoras de escritorio
  DHT11 module: https://cdn-learn.adafruit.com/downloads/pdf/dht.pdf DHT11 black pcb module reference by:https://github.com/adafruit/Fritzing-Library/blob/master/parts/DHT11%20Humitidy%20and%20Temperature%20Sensor.fzpz
  LCM1602 IIC: I2C-Module to use a 1602 or 2004 LCD on with the wire.h libory Serial LCD Modul
